# Fritzing sketch schematic (saved by Fritzing 1.0.4)
breadboards: 2

parts:
  Part1 = Arduino Uno (Rev3) - ICSP
  R1 = Resistor [tolerance=±5% resistance=20k package="0603 [SMD]"]
  R3 = Resistor [tolerance=±5% resistance=20k package="2512 [SMD]"]
  R4 = Resistor [tolerance=±5% resistance=10k package="2512 [SMD]"]
  R5 = Resistor [tolerance=±5% resistance=10k package="2512 [SMD]"]
  R6 = Resistor [tolerance=±5% resistance=10k package="2512 [SMD]"]
  R7 = Resistor [tolerance=±5% resistance=10k package="2512 [SMD]"]
  R8 = Resistor [tolerance=±5% resistance=10k package="2512 [SMD]"]
  R9 = Resistor [tolerance=±5% resistance=10k package="2512 [SMD]"]
  R10 = Resistor [tolerance=±5% resistance=10k package="2512 [SMD]"]
  R11 = Resistor [tolerance=±5% resistance=20k package="2512 [SMD]"]
  R12 = Resistor [tolerance=±5% resistance=20k package="2512 [SMD]"]
  R13 = Resistor [tolerance=±5% resistance=20k package="2512 [SMD]"]
  R14 = Resistor [tolerance=±5% resistance=20k package="2512 [SMD]"]
  R15 = Resistor [tolerance=±5% resistance=20k package="2512 [SMD]"]
  R16 = Resistor [tolerance=±5% resistance=20k package="2512 [SMD]"]
  R17 = Resistor [tolerance=±5% resistance=20k package="2512 [SMD]"]
  C1 = Ceramic Capacitor [capacitance=47nF voltage=35V package="100 mil [THT, multilayer]"]
  U1 = Stereo 3.7W Class D Amplifier [package=14-tdfn]
  RE1 = Rotary Encoder [package=THT]
  R18 = Resistor [tolerance=±5% resistance=1k package="0603 [SMD]"]
  R19 = Resistor [tolerance=±5% resistance=1k package="0603 [SMD]"]
  R20 = Resistor [tolerance=±5% resistance=10k package="0603 [SMD]"]
  LED1 = RGB LED (com. anode, rbg) [color="Red (633nm)" current=0.030A package="5 mm [THT]"]
  C2 = Ceramic Capacitor [capacitance=100nF voltage=35V package="100 mil [THT, multilayer]"]
  SP1 = SPEAKER [package=pcb_mount_speaker]
  TRS1 = Audio Jack (TRS) 3.5mm [package="PG203J [THT]"]
  R21 = Resistor [tolerance=±5% resistance=100M package="0603 [SMD]"]
  C4 = Ceramic Capacitor [capacitance=6.8nF voltage=35V package="100 mil [THT, multilayer]"]
  C5 = Ceramic Capacitor [capacitance=10µF voltage=35V package="100 mil [THT, multilayer]"]
  R22 = Resistor [tolerance=±5% resistance=100M package="0603 [SMD]"]

nets:
  N1: Part1.A0, Part1.5V, U1.INR+, U1.OUTR+, R22.Pin_1
  N2: Part1.D8, RE1.EncoderPinB
  N3: Part1.D9_PWM, RE1.EncoderPinC
  N4: Part1.D10_PWM/SS, R19.Pin_0
  N5: Part1.D11_PWM/MOSI, R18.Pin_0
  N6: Part1.D12/MISO, RE1.EncoderPinA
  N7: Part1.D13/SCK, R20.Pin_0
  N8: Part1.AREF, C2.0
  N9: Part1.D0/RX, R3.Pin_0
  N10: Part1.D1/TX, R11.Pin_0
  N11: Part1.D2, R12.Pin_0
  N12: Part1.D3_PWM, R13.Pin_0
  N13: Part1.D4, R14.Pin_0
  N14: Part1.D5_PWM, R15.Pin_0
  N15: Part1.D6_PWM, R16.Pin_0
  N16: Part1.D7, R17.Pin_0
  GND: Part1.GND, R1.Pin_1, C1.1, U1.GND, U1.SHDN, U1.OUTR-, C2.1, TRS1.Ring, R21.Pin_1, C4.1, C5.0
  N17: R1.Pin_0, R3.Pin_1, R4.Pin_0
  N18: R4.Pin_1, R5.Pin_0, R11.Pin_1
  N19: R5.Pin_1, R7.Pin_0, R12.Pin_1
  N20: R6.Pin_0, R7.Pin_1, R13.Pin_1
  N21: R6.Pin_1, R8.Pin_0, R14.Pin_1
  N22: R8.Pin_1, R9.Pin_0, R15.Pin_1
  N23: R9.Pin_1, R10.Pin_0, R16.Pin_1
  N24: R10.Pin_1, R17.Pin_1, C1.0
  N25: U1.INL+, U1.OUTL-, SP1.+
  N26: U1.INL-, U1.OUTL+, SP1.-
  N27: U1.GAIN, U1.INR-, U1.VDD
  N28: R18.Pin_1, LED1.red_cathode
  N29: R19.Pin_1, LED1.green_cathode
  N30: R20.Pin_1, LED1.blue_cathode
  N31: R21.Pin_0, C4.0, C5.1, R22.Pin_0
